# Fritzing sketch Untitled Sketch (saved by Fritzing 0.9.3b)
breadboards: 1

parts:
  Part1 = Arduino Mega 2560 (Rev3)
  J1 = Basic Servo
  J2 = Basic Servo
  J3 = Basic Servo
  J4 = Basic Servo
  J5 = Basic Servo
  J6 = Basic Servo
  J7 = Basic Servo
  J8 = Basic Servo
  J9 = Basic Servo
  J10 = Basic Servo
  J11 = Basic Servo
  J12 = Basic Servo

nets:
  N1: Part1.D21/SCL, J4.pulse
  N2: Part1.D19/RX1, J12.pulse
  N3: Part1.D15/RX3, J10.pulse
  N4: Part1.D14/TX3, J11.pulse
  N5: Part1.D9_PWM, J3.pulse
  GND: Part1.GND, J2.gnd, J4.gnd, J5.gnd, J6.gnd, J7.gnd, J8.gnd, J11.gnd
  N6: Part1.D0_RX0, J9.pulse
  N7: Part1.D3_PWM, J8.pulse
  N8: Part1.D5_PWM, J5.pulse
  VCC: Part1.5V, J1.vcc, J2.vcc, J3.vcc, J4.vcc, J5.vcc, J6.vcc, J7.vcc, J8.vcc, J10.vcc, J11.vcc, J12.vcc
